# Fritzing sketch Layout (saved by Fritzing 0.9.3b)
stripboards: 1
breadboards: 1

parts:
  Part1 = Arduino Uno (Rev3) - ICSP
  Part2 = NRF24L01+ Breakout Board  # not connected
  LED1 = LED - 5mm [color="Red (633nm)" package="5 mm [THT]"]

nets:
  N1: Part1.D6_PWM, LED1.anode
  N2: Part1.5V, LED1.cathode

// code stored in the sketch: Test.ino
void setup() {

}

void loop() {

	digitalWrite(6, HIGH);
	delay(500);
	digitalWrite(6, LOW);
	delay(500);

}
